# Fritzing sketch fritzing (saved by Fritzing 0.8.7b)
breadboards: 1

parts:
  Raspberry_Pi_B_rev1 = Raspberry Pi B rev1
  DHT1 = DHT22 Humidity and Temperature Sensor
  IC1 = MCP3008 8-channel 10-bit ADC [part_number=MCP3008]
  U1 = TMP36 [package=to-92-kit]
  R1 = Resistor [tolerance=±5% resistance=10k package=THT]

nets:
  3V3: Raspberry_Pi_B_rev1.3V3, DHT1.VDD, IC1.no_name_yet#15, IC1.no_name_yet#16, U1.VCC, R1.Pin_1
  GND: Raspberry_Pi_B_rev1.GND, DHT1.GND, IC1.no_name_yet#9, IC1.no_name_yet#14, U1.GND
  N1: Raspberry_Pi_B_rev1.GPIO_4, DHT1.DATA, R1.Pin_0
  N2: Raspberry_Pi_B_rev1.GPIO_10, IC1.no_name_yet#11
  N3: Raspberry_Pi_B_rev1.GPIO_9, IC1.no_name_yet#12
  N4: Raspberry_Pi_B_rev1.GPIO_11, IC1.no_name_yet#13
  N5: Raspberry_Pi_B_rev1.GPIO_8, IC1.no_name_yet#10
  N6: IC1.no_name_yet#1, U1.VOUT
